# Fritzing sketch bongo_hero (saved by Fritzing 0.9.3b)
breadboards: 1

parts:
  Composant1 = Arduino Uno (Rev3)
  Composant2 = ws2812b [package="smd 2812b"]
  J1 = Piezo Speaker
  R1 = Resistor [tolerance=±5% resistance=1M package=THT]
  R2 = Resistor [tolerance=±5% resistance=220 package=THT]

nets:
  N1: Composant1.A0, R2.Pin_0
  GND: Composant1.GND, Composant2.VSS, J1.pin1
  N2: Composant1.D2, R1.Pin_1
  5V: Composant1.5V, Composant2.VDD
  N3: Composant2.DIN, R1.Pin_0
  N4: J1.pin2, R2.Pin_1
